# Fritzing sketch Wiring (saved by Fritzing 1.0.5)
circuit board: 8.41894cm x 5.60626cm

parts:
  0_96"_OLED = ESP8266 nodemcu 0.96in OLED display
  U1 = LIPO-110mAh [package=lipo-110]
  Charger_Module_TP4056 = TP4056 [chip_label=TP4056 package="DIP (Dual Inline) [THT]"]
  Slide_Switch_SPDT_3_PIN = Toggle Switch [package=THT]
  M1 = BME680 Module [part_number=CJMCU-680]

nets:
  N1: 0_96"_OLED.Pin_2, 0_96"_OLED.Pin_14, 0_96"_OLED.Pin_17, 0_96"_OLED.Pin_24, Charger_Module_TP4056.pin6, M1.GND, M1.SDO
  N2: 0_96"_OLED.Pin_15, Slide_Switch_SPDT_3_PIN.L1
  N3: 0_96"_OLED.Pin_22, M1.SCL
  N4: 0_96"_OLED.Pin_23, M1.SDA
  N5: 0_96"_OLED.Pin_25, M1.VCC
  N6: U1.+, Charger_Module_TP4056.pin4
  N7: U1.-, Charger_Module_TP4056.pin5
  N8: Charger_Module_TP4056.pin3, Slide_Switch_SPDT_3_PIN.COM

custom parts:
  ESP8266 nodemcu 0.96in OLED display: The board integrates an ESP8266 NodeMCU and a 0.96-inch OLED screen, providing all the functionality of a traditional ESP8266 module with the same size and peripheral ports, as well as higher-performance development tools and high-definition data display.
  TP4056: A DIP stand-in part for whatever IC you want. With 6 pins on a 300mil dual inline package (DIP) footprint.
  BME680 Module: Bosch BME680 Development Module The BME680 is a digital 4-in-1 sensor that measures air quality [gas], humidity, pressure and temperature. Links: BME680 product datasheet
